// Logisim project Jing1632.circ as structural Verilog
module FullAdder (
  input  A,
  input  B,
  input  Cin,
  output Sum,
  output Cout
);

  wire and_1_out, and_2_out, and_3_out;

  xor xor_1 (Sum, A, B, Cin);
  and and_1 (and_1_out, A, B);
  and and_2 (and_2_out, A, Cin);
  and and_3 (and_3_out, B, Cin);
  or or_1 (Cout, and_1_out, and_2_out, and_3_out);
endmodule

module RCA4 (
  input  [3:0] A,
  input  [3:0] B,
  input  Cin,
  output [3:0] Sum,
  output Cout
);

  wire FullAdder_1_cout, FullAdder_2_cout, FullAdder_3_cout;

  FullAdder FullAdder_1 (.A(A[0]), .B(B[0]), .Cin(Cin), .Sum(Sum[0]), .Cout(FullAdder_1_cout));
  FullAdder FullAdder_2 (.A(A[1]), .B(B[1]), .Cin(FullAdder_1_cout), .Sum(Sum[1]), .Cout(FullAdder_2_cout));
  FullAdder FullAdder_3 (.A(A[2]), .B(B[2]), .Cin(FullAdder_2_cout), .Sum(Sum[2]), .Cout(FullAdder_3_cout));
  FullAdder FullAdder_4 (.A(A[3]), .B(B[3]), .Cin(FullAdder_3_cout), .Sum(Sum[3]), .Cout(Cout));
endmodule

module RCA16 (
  input  [15:0] A,
  input  [15:0] B,
  input  Cin,
  output [15:0] Sum,
  output Cout
);

  wire RCA4_1_cout, RCA4_2_cout, RCA4_3_cout;

  RCA4 RCA4_1 (.A(A[3:0]), .B(B[3:0]), .Cin(Cin), .Sum(Sum[3:0]), .Cout(RCA4_1_cout));
  RCA4 RCA4_2 (.A(A[7:4]), .B(B[7:4]), .Cin(RCA4_1_cout), .Sum(Sum[7:4]), .Cout(RCA4_2_cout));
  RCA4 RCA4_3 (.A(A[11:8]), .B(B[11:8]), .Cin(RCA4_2_cout), .Sum(Sum[11:8]), .Cout(RCA4_3_cout));
  RCA4 RCA4_4 (.A(A[15:12]), .B(B[15:12]), .Cin(RCA4_3_cout), .Sum(Sum[15:12]), .Cout(Cout));
endmodule

module RCA1632 (
  input  [31:0] A32,
  input  Cin,
  input  [31:0] B32,
  input  Enable32,
  output [31:0] Sum1632,
  output Cout1632
);

  wire controlled_buffer_3_out, RCA16_1_cout, RCA16_2_cout;
  wire [15:0] controlled_buffer_1_out, controlled_buffer_2_out;

  assign controlled_buffer_1_out = Enable32 ? A32[31:16] : 16'bz;  // Controlled_Buffer controlled_buffer_1
  assign controlled_buffer_2_out = Enable32 ? B32[31:16] : 16'bz;  // Controlled_Buffer controlled_buffer_2
  assign controlled_buffer_3_out = Enable32 ? RCA16_1_cout : 1'bz;  // Controlled_Buffer controlled_buffer_3
  RCA16 RCA16_1 (.A(A32[15:0]), .B(B32[15:0]), .Cin(Cin), .Sum(Sum1632[15:0]), .Cout(RCA16_1_cout));
  RCA16 RCA16_2 (
    .A(controlled_buffer_1_out), .B(controlled_buffer_2_out), .Cin(controlled_buffer_3_out),
    .Sum(Sum1632[31:16]), .Cout(RCA16_2_cout));
  Multiplexer multiplexer_1 (.in0(RCA16_1_cout), .in1(RCA16_2_cout), .out(Cout1632), .sel(Enable32));
endmodule

module Increment1632 (
  input  [31:0] in32,
  input  Enable32,
  output [31:0] out32
);

  RCA1632 RCA1632_1 (.A32(in32), .Cin(1'b1), .Enable32(Enable32), .Sum1632(out32));  // open: B32, Cout1632
endmodule

module Bit (
  input  Bit_in,
  input  BitLoad,
  output BitOut
);

  wire clock_1_out, multiplexer_1_out;

  D_Flip_Flop d_ff_1 (.D(multiplexer_1_out), .clk(clock_1_out), .Q(BitOut));  // open: Qn, preset, reset
  Multiplexer multiplexer_1 (.in0(BitOut), .in1(Bit_in), .out(multiplexer_1_out), .sel(BitLoad));
  Clock clock_1 (.out(clock_1_out));
endmodule

module Register16 (
  input  [15:0] In16,
  input  Load,
  input  clk,
  output [15:0] Out16
);

  wire [15:0] multiplexer_1_out;

  Multiplexer #(.width(16)) multiplexer_1 (.in0(Out16), .in1(In16), .out(multiplexer_1_out), .sel(Load));
  D_Flip_Flop d_ff_1 (.D(multiplexer_1_out[0]), .clk(clk), .Q(Out16[0]));  // open: Qn, preset, reset
  D_Flip_Flop d_ff_2 (.D(multiplexer_1_out[1]), .clk(clk), .Q(Out16[1]));  // open: Qn, preset, reset
  D_Flip_Flop d_ff_3 (.D(multiplexer_1_out[2]), .clk(clk), .Q(Out16[2]));  // open: Qn, preset, reset
  D_Flip_Flop d_ff_4 (.D(multiplexer_1_out[3]), .clk(clk), .Q(Out16[3]));  // open: Qn, preset, reset
  D_Flip_Flop d_ff_5 (.D(multiplexer_1_out[4]), .clk(clk), .Q(Out16[4]));  // open: Qn, preset, reset
  D_Flip_Flop d_ff_6 (.D(multiplexer_1_out[5]), .clk(clk), .Q(Out16[5]));  // open: Qn, preset, reset
  D_Flip_Flop d_ff_7 (.D(multiplexer_1_out[6]), .clk(clk), .Q(Out16[6]));  // open: Qn, preset, reset
  D_Flip_Flop d_ff_8 (.D(multiplexer_1_out[7]), .clk(clk), .Q(Out16[7]));  // open: Qn, preset, reset
  D_Flip_Flop d_ff_9 (.D(multiplexer_1_out[8]), .clk(clk), .Q(Out16[8]));  // open: Qn, preset, reset
  D_Flip_Flop d_ff_10 (.D(multiplexer_1_out[9]), .clk(clk), .Q(Out16[9]));  // open: Qn, preset, reset
  D_Flip_Flop d_ff_11 (.D(multiplexer_1_out[10]), .clk(clk), .Q(Out16[10]));  // open: Qn, preset, reset
  D_Flip_Flop d_ff_12 (.D(multiplexer_1_out[11]), .clk(clk), .Q(Out16[11]));  // open: Qn, preset, reset
  D_Flip_Flop d_ff_13 (.D(multiplexer_1_out[12]), .clk(clk), .Q(Out16[12]));  // open: Qn, preset, reset
  D_Flip_Flop d_ff_14 (.D(multiplexer_1_out[13]), .clk(clk), .Q(Out16[13]));  // open: Qn, preset, reset
  D_Flip_Flop d_ff_15 (.D(multiplexer_1_out[14]), .clk(clk), .Q(Out16[14]));  // open: Qn, preset, reset
  D_Flip_Flop d_ff_16 (.D(multiplexer_1_out[15]), .clk(clk), .Q(Out16[15]));  // open: Qn, preset, reset
endmodule

module Register32 (
  input  [31:0] in32,
  input  Load,
  input  clk,
  output [31:0] out32
);

  Register16 Register16_1 (.In16(in32[15:0]), .Load(Load), .clk(clk), .Out16(out32[15:0]));
  Register16 Register16_2 (.In16(in32[31:16]), .Load(Load), .clk(clk), .Out16(out32[31:16]));
endmodule

module PC1632 (
  input  clk,
  input  inc,
  input  load,
  input  reset,
  input  [31:0] in16,
  output [31:0] out32
);

  wire [31:0] Increment1632_1_out32, multiplexer_1_out, multiplexer_2_out, multiplexer_3_out;

  Increment1632 Increment1632_1 (.in32(out32), .Enable32(1'b1), .out32(Increment1632_1_out32));
  Multiplexer #(.width(32)) multiplexer_1 (
    .in0(out32), .in1(Increment1632_1_out32), .out(multiplexer_1_out), .sel(inc));
  Multiplexer #(.width(32)) multiplexer_2 (.in0(multiplexer_1_out), .in1(in16), .out(multiplexer_2_out), .sel(load));
  Multiplexer #(.width(32)) multiplexer_3 (
    .in0(multiplexer_2_out), .in1({32{1'b0}}), .out(multiplexer_3_out), .sel(reset));
  Register32 Register32_1 (.in32(multiplexer_3_out), .Load(1'b1), .clk(clk), .out32(out32));
endmodule

module LogicUnit (
  input  Enable32,
  input  [31:0] A32,
  input  [31:0] B32,
  input  [1:0] F,
  output [31:0] Y32
);

  wire [15:0] controlled_buffer_1_out, controlled_buffer_2_out, multiplexer_1_out, multiplexer_2_out;
  wire [31:0] and_1_out, or_1_out, xor_1_out;

  assign controlled_buffer_1_out = Enable32 ? A32[31:16] : 16'bz;  // Controlled_Buffer controlled_buffer_1
  assign controlled_buffer_2_out = Enable32 ? B32[31:16] : 16'bz;  // Controlled_Buffer controlled_buffer_2
  Multiplexer #(.width(16)) multiplexer_1 (
    .in0({16{1'b0}}), .in1(controlled_buffer_1_out), .out(multiplexer_1_out), .sel(Enable32));
  Multiplexer #(.width(16)) multiplexer_2 (
    .in0({16{1'b0}}), .in1(controlled_buffer_2_out), .out(multiplexer_2_out), .sel(Enable32));
  assign and_1_out = {multiplexer_1_out, A32[15:0]} & {multiplexer_2_out, B32[15:0]};  // AND_Gate and_1, 32 bits wide
  assign or_1_out = {multiplexer_1_out, A32[15:0]} | {multiplexer_2_out, B32[15:0]};  // OR_Gate or_1, 32 bits wide
  assign xor_1_out = {multiplexer_1_out, A32[15:0]} ^ {multiplexer_2_out, B32[15:0]};  // XOR_Gate xor_1, 32 bits wide
  Multiplexer #(.select(2), .width(32)) multiplexer_3 (
    .in0(and_1_out), .in1(or_1_out), .in2(xor_1_out), .in3({multiplexer_2_out, B32[15:0]}), .out(Y32), .sel(F));
endmodule

module ALU1632 (
  input  [31:0] A,
  input  [31:0] B,
  input  [3:0] opcode,
  input  Enable32,
  output [31:0] Out32,
  output N,
  output Z,
  output C
);

  wire or_1_out;
  wire [31:0] LogicUnit_1_y32, multiplexer_1_out, multiplexer_2_out, not_1_out, not_2_out, RCA1632_1_sum1632;

  assign not_1_out = ~A;  // NOT_Gate not_1, 32 bits wide
  assign not_2_out = ~B;  // NOT_Gate not_2, 32 bits wide
  Multiplexer #(.width(32)) multiplexer_1 (.in0(A), .in1(not_1_out), .out(multiplexer_1_out), .sel(opcode[0]));
  Multiplexer #(.width(32)) multiplexer_2 (.in0(B), .in1(not_2_out), .out(multiplexer_2_out), .sel(opcode[1]));
  RCA1632 RCA1632_1 (
    .A32(multiplexer_1_out), .Cin(opcode[2]), .B32(multiplexer_2_out), .Enable32(Enable32),
    .Sum1632(RCA1632_1_sum1632), .Cout1632(C));
  LogicUnit LogicUnit_1 (
    .Enable32(Enable32), .A32(multiplexer_1_out), .B32(multiplexer_2_out), .F({opcode[2], opcode[0]}),
    .Y32(LogicUnit_1_y32));
  Multiplexer #(.width(32)) multiplexer_3 (
    .in0(RCA1632_1_sum1632), .in1(LogicUnit_1_y32), .out({N, Out32[30:0]}), .sel(opcode[3]));
  or or_1 (or_1_out, Out32[0], Out32[1], Out32[2], Out32[3], Out32[4], Out32[5], Out32[6], Out32[7], Out32[8], Out32[9], Out32[10], Out32[11], Out32[12], Out32[13], Out32[14], Out32[15], Out32[17], Out32[18], Out32[19], Out32[20], Out32[21], Out32[22], Out32[23], Out32[24], Out32[25], Out32[26], Out32[27], Out32[28], Out32[29], Out32[30], N, Out32[16]);
  not not_3 (Z, or_1_out);

  assign Out32[31] = N;
endmodule

module RegisterBank (
  input  [31:0] in32,
  input  Write,
  input  [2:0] Rd,
  input  [2:0] Ra,
  input  [2:0] Rb,
  input  clk,
  output [31:0] out32a,
  output [31:0] out32b
);

  wire demultiplexer_1_out0, demultiplexer_1_out1, demultiplexer_1_out2, demultiplexer_1_out3,
       demultiplexer_1_out4, demultiplexer_1_out5, demultiplexer_1_out6, demultiplexer_1_out7;
  wire [31:0] Register32_1_out32, Register32_2_out32, Register32_3_out32, Register32_4_out32,
       Register32_5_out32, Register32_6_out32, Register32_7_out32, Register32_8_out32;

  Demultiplexer #(.select(3)) demultiplexer_1 (
    .out0(demultiplexer_1_out0), .out1(demultiplexer_1_out1), .out2(demultiplexer_1_out2),
    .out3(demultiplexer_1_out3), .out4(demultiplexer_1_out4), .out5(demultiplexer_1_out5),
    .out6(demultiplexer_1_out6), .out7(demultiplexer_1_out7), .in(Write), .sel(Rd));
  Register32 Register32_1 (.in32(in32), .Load(demultiplexer_1_out0), .clk(clk), .out32(Register32_1_out32));
  Register32 Register32_2 (.in32(in32), .Load(demultiplexer_1_out1), .clk(clk), .out32(Register32_2_out32));
  Register32 Register32_3 (.in32(in32), .Load(demultiplexer_1_out2), .clk(clk), .out32(Register32_3_out32));
  Register32 Register32_4 (.in32(in32), .Load(demultiplexer_1_out3), .clk(clk), .out32(Register32_4_out32));
  Register32 Register32_5 (.in32(in32), .Load(demultiplexer_1_out4), .clk(clk), .out32(Register32_5_out32));
  Register32 Register32_6 (.in32(in32), .Load(demultiplexer_1_out5), .clk(clk), .out32(Register32_6_out32));
  Register32 Register32_7 (.in32(in32), .Load(demultiplexer_1_out6), .clk(clk), .out32(Register32_7_out32));
  Register32 Register32_8 (.in32(in32), .Load(demultiplexer_1_out7), .clk(clk), .out32(Register32_8_out32));
  Multiplexer #(.select(3), .width(32)) multiplexer_1 (
    .in0(Register32_1_out32), .in1(Register32_2_out32), .in2(Register32_3_out32), .in3(Register32_4_out32),
    .in4(Register32_5_out32), .in5(Register32_6_out32), .in6(Register32_7_out32), .in7(Register32_8_out32),
    .out(out32a), .sel(Ra));
  Multiplexer #(.select(3), .width(32)) multiplexer_2 (
    .in0(Register32_1_out32), .in1(Register32_2_out32), .in2(Register32_3_out32), .in3(Register32_4_out32),
    .in4(Register32_5_out32), .in5(Register32_6_out32), .in6(Register32_7_out32), .in7(Register32_8_out32),
    .out(out32b), .sel(Rb));
endmodule

module BarrelShifter (
  input  [31:0] in32,
  input  [4:0] shiftby,
  input  [2:0] f,
  output [31:0] out32
);

  wire [31:0] demultiplexer_1_out0, demultiplexer_1_out1, demultiplexer_1_out2, demultiplexer_1_out3,
       demultiplexer_1_out4, demultiplexer_1_out5, shifter_1_out, shifter_2_out, shifter_3_out,
       shifter_4_out, shifter_5_out;

  Demultiplexer #(.select(3), .width(32)) demultiplexer_1 (
    .out0(demultiplexer_1_out0), .out1(demultiplexer_1_out1), .out2(demultiplexer_1_out2),
    .out3(demultiplexer_1_out3), .out4(demultiplexer_1_out4), .out5(demultiplexer_1_out5), .in(in32), .sel(f));  // open: out6, out7
  Shifter #(.width(32)) shifter_1 (.in(demultiplexer_1_out1), .\dist (shiftby), .out(shifter_1_out));
  Shifter #(.shift("lr"), .width(32)) shifter_2 (.in(demultiplexer_1_out2), .\dist (shiftby), .out(shifter_2_out));
  Shifter #(.shift("ar"), .width(32)) shifter_3 (.in(demultiplexer_1_out3), .\dist (shiftby), .out(shifter_3_out));
  Shifter #(.shift("rl"), .width(32)) shifter_4 (.in(demultiplexer_1_out4), .\dist (shiftby), .out(shifter_4_out));
  Shifter #(.shift("rr"), .width(32)) shifter_5 (.in(demultiplexer_1_out5), .\dist (shiftby), .out(shifter_5_out));
  Multiplexer #(.select(3), .width(32)) multiplexer_1 (
    .in0(demultiplexer_1_out0), .in1(shifter_1_out), .in2(shifter_2_out), .in3(shifter_3_out),
    .in4(shifter_4_out), .in5(shifter_5_out), .out(out32), .sel(f));  // open: in6, in7
endmodule

module CPU (
  input  Input_1,
  input  Increment,
  input  Reset
);

  wire ALU1632_1_c, ALU1632_1_n, ALU1632_1_z, and_1_out, and_2_out, and_3_out, and_4_out, BranchAllow,
       BranchLoad, clk, Data, Load, LoadL, not_1_out, or_1_out, or_2_out, Shift, Store;
  wire [1:0] BranchControl, controlled_buffer_8_out;
  wire [2:0] controlled_buffer_3_out, controlled_buffer_7_out, Rb;
  wire [9:0] Addr;
  wire [15:0] BranchAddress, multiplexer_2_out, RAM_1_data, RAM_1_data_2;
  wire [31:0] ALU1632_1_out32, BarrelShifter_1_out32, controlled_buffer_1_out, multiplexer_3_out,
       PC1632_1_out32, RegisterBank_1_out32a, RegisterBank_1_out32b, ROM_1_data;
  wire [31:16] controlled_buffer_6_out;

  Clock clock_1 (.out(clk));
  RAM #(.addrWidth(10), .dataWidth(32), .databus("bidir")) RAM_1 (
    .addr(Addr), .we(Store), .oe(Load), .clk(clk), .data({RAM_1_data, RAM_1_data_2}));
  Multiplexer #(.width(16)) multiplexer_1 (
    .in0({16{1'b0}}), .in1(controlled_buffer_6_out), .out(RAM_1_data), .sel(Input_1));
  Multiplexer #(.width(16)) multiplexer_2 (.in0({16{1'b0}}), .in1(RAM_1_data), .out(multiplexer_2_out), .sel(Input_1));
  assign controlled_buffer_1_out = Data ? ALU1632_1_out32 : 32'bz;  // Controlled_Buffer controlled_buffer_1
  assign controlled_buffer_1_out = Load ? {multiplexer_2_out, RAM_1_data_2} : 32'bz;  // Controlled_Buffer controlled_buffer_2
  assign controlled_buffer_3_out = or_1_out ? Rb : 3'bz;  // Controlled_Buffer controlled_buffer_3
  or or_1 (or_1_out, LoadL, Load);
  assign controlled_buffer_1_out = LoadL ? {{24{1'b0}}, Addr[7:0]} : 32'bz;  // Controlled_Buffer controlled_buffer_4
  assign controlled_buffer_3_out = Data ? Addr[5:3] : 3'bz;  // Controlled_Buffer controlled_buffer_5
  assign {controlled_buffer_6_out, RAM_1_data_2} = Store ? RegisterBank_1_out32b : 32'bz;  // Controlled_Buffer controlled_buffer_6
  or or_2 (or_2_out, Data, Load, LoadL);
  PC1632 PC1632_1 (
    .clk(clk), .inc(Increment), .load(BranchLoad), .reset(Reset), .in16({{16{1'b0}}, BranchAddress}),
    .out32(PC1632_1_out32));
  RegisterBank RegisterBank_1 (
    .in32(controlled_buffer_1_out), .Write(or_2_out), .Rd(controlled_buffer_3_out), .Ra(Addr[2:0]), .Rb(Rb),
    .clk(clk), .out32a(RegisterBank_1_out32a), .out32b(RegisterBank_1_out32b));
  ROM #(.addrWidth(16), .dataWidth(32)) ROM_1 (.addr(PC1632_1_out32[15:0]), .data(ROM_1_data));
  assign controlled_buffer_7_out = Shift ? BranchAddress[6:4] : 3'bz;  // Controlled_Buffer controlled_buffer_7
  BarrelShifter BarrelShifter_1 (
    .in32(RegisterBank_1_out32b), .shiftby(BranchAddress[11:7]), .f(controlled_buffer_7_out),
    .out32(BarrelShifter_1_out32));
  Multiplexer #(.width(32)) multiplexer_3 (
    .in0({{16{1'b0}}, ROM_1_data[15:0]}), .in1(ROM_1_data), .out(multiplexer_3_out), .sel(Input_1));
  ALU1632 ALU1632_1 (
    .A(RegisterBank_1_out32a), .B(BarrelShifter_1_out32), .opcode(Addr[9:6]), .Enable32(Input_1),
    .Out32(ALU1632_1_out32), .N(ALU1632_1_n), .Z(ALU1632_1_z), .C(ALU1632_1_c));
  Multiplexer #(.select(2)) multiplexer_4 (
    .in0(1'b1), .in1(ALU1632_1_n), .in2(ALU1632_1_z), .in3(ALU1632_1_c), .out(BranchLoad),
    .sel(controlled_buffer_8_out));
  assign controlled_buffer_8_out = BranchAllow ? BranchControl : 2'bz;  // Controlled_Buffer controlled_buffer_8
  Register32 Register32_1 (
    .in32(multiplexer_3_out), .Load(1'b1), .clk(clk),
    .out32({BranchAllow, BranchControl, BranchAddress, Addr, Rb}));
  and and_1 (and_1_out, ~BranchAddress[2], ~BranchAddress[1], BranchAddress[0]);  // AND_Gate
  and and_2 (and_2_out, ~BranchAddress[2], BranchAddress[1], ~BranchAddress[0]);  // AND_Gate
  and and_3 (and_3_out, BranchAddress[2], ~BranchAddress[1], ~BranchAddress[0]);  // AND_Gate
  and and_4 (and_4_out, ~BranchAddress[2], BranchAddress[1], BranchAddress[0]);  // AND_Gate
  assign Shift = not_1_out ? BranchAddress[3] : 1'bz;  // Controlled_Buffer controlled_buffer_9
  assign Data = not_1_out ? and_1_out : 1'bz;  // Controlled_Buffer controlled_buffer_10
  assign Load = not_1_out ? and_2_out : 1'bz;  // Controlled_Buffer controlled_buffer_11
  assign Store = not_1_out ? and_3_out : 1'bz;  // Controlled_Buffer controlled_buffer_12
  assign LoadL = not_1_out ? and_4_out : 1'bz;  // Controlled_Buffer controlled_buffer_13
  not not_1 (not_1_out, BranchAllow);

  // Other names for the same wires on the sheet: ShiftType[2:0] = BranchAddress[6:4];
  //   ShiftBy[4:0] = BranchAddress[11:7]; op[3:0] = Addr[9:6]; Enable32 = Input_1; Ra[2:0] = Addr[2:0];
  //   Value[7:0] = Addr[7:0]; Rd[2:0] = Addr[5:3]

  // Notes on the sheet:
  //   Data Memory
  //   Program Counter
  //   contents of ROM_1 (hex, n*v repeats v):
  //   6020 6059 432081 80032000 21*0 8000 8009 8012
  //   Instruction Memory
  //   Instruction Register
endmodule
